# Fritzing sketch 5V Regulator (saved by Fritzing 0.9.2b)
breadboards: 1

parts:
  Power_plug_(6V-12V) = Power plug
  USB_female_plug = USB Connectors [package=usb-a-s-nosilk]
  part = USB Connectors [package=usb-a-s-nosilk]
  LM2940T-5_0 = Voltage Regulator [package=to-220-alt]
  part_2 = Electrolytic Capacitor [capacitance=100µF package="200 mil [THT, electrolytic]"]
  part_3 = Electrolytic Capacitor [capacitance=10µF package="200 mil [THT, electrolytic]"]
  part_4 = Resistor [tolerance=±5% resistance=220 package="2512 [SMD]"]
  part_5 = smd LED [color="Red (633nm)" package="0603 [SMD]"]
  Switch = Square Pushbutton

nets:
  GND: Power_plug_(6V-12V).GND, USB_female_plug.GND, part.GND, LM2940T-5_0.GND, part_2.-, part_3.-, part_5.cathode
  N1: Power_plug_(6V-12V).VCC, LM2940T-5_0.IN, part_2.+
  N2: USB_female_plug.D+, part.D+, LM2940T-5_0.OUT, part_3.+, Switch.leg1
  N3: part_4.Pin_0, Switch.leg0
  N4: part_4.Pin_1, part_5.anode
